# Fritzing sketch Snake Schematic (saved by Fritzing 0.9.3b)
breadboards: 1

parts:
  Part1 = Arduino Due (Rev2b)
  Part2 = Matrix LED de 8x8 basada en MAX7219
  Part4 = Thumb Joystick

nets:
  N1: Part1.A0, Part4.VRy
  N2: Part1.A1, Part4.VRx
  5V: Part1.5V, Part2.VCC, Part4.5V
  GND: Part1.GND, Part2.GND, Part4.GND
  N3: Part1.D8_PWM, Part4.SW
  N4: Part1.D10_PWM/SS0, Part2.CS
  N5: Part1.D11_PWM, Part2.CLK
  N6: Part1.D12_PWM, Part2.DIN

custom parts:
  Thumb Joystick: Description: This is the breakout board for the thumb joystick. Pins are broken out to a 0.1" header and includes 4 mounting holes in the corners. Dimensions: 1" x 1.25"
